// Logisim project SAPER.circ as structural Verilog: 1 circuit, main circuit main
module main (
  input  [3:0] Adres,
  output [3:0] out_2,
  output [5:0] out_3,
  output koniec_gry
);

  wire clock_1_out, clock_2_out, E1, M1, main_2_out_10, not_1_out, not_2_out, START_out;
  wire [1:0] main_1_out_2;
  wire [3:0] controlled_buffer_2_out, ram_1_data;
  wire [4:0] X1, Y1;
  wire [5:0] main_1_out_3;
  wire [6:0] keyboard_1_data;
  wire [24:0] \sterowanie_dużo_1_nr_zaznaczonego_pola ;
  wire [30:0] main_3_out_7, main_3_out_8, main_3_out_9, main_3_out_10, main_3_out_11, main_3_out_12,
       main_3_out_13, main_3_out_14, main_3_out_15, main_3_out_16, main_3_out_17, main_3_out_18,
       main_3_out_19, main_3_out_20, main_3_out_21, main_3_out_22, main_3_out_23, main_3_out_24,
       main_3_out_25, main_3_out_26, main_3_out_27, main_3_out_28, main_3_out_29, main_3_out_30,
       main_3_out_31, main_3_out_32, main_3_out_33, main_3_out_34, main_3_out_35, main_3_out_36,
       main_3_out_37;

  Maszyna_Los_XY22_main main_1 (.START(START_out), .out_3(main_1_out_3), .out_2(main_1_out_2));
  Clock clock_1 (.out(clock_1_out));
  Keyboard #(.buflen(1)) keyboard_1 (.clk(clock_1_out), .data(keyboard_1_data));  // open: re, clr, avail
  Clock #(.lowDuration(4)) clock_2 (.out(clock_2_out));
  \porównywacz_main  main_2 (
    .in_1(main_1_out_2), .in_2(main_1_out_3), .in_3(START_out), .in_7(E1), .out_8(out_2), .in_4(Y1),
    .in_5(X1), .out_10(main_2_out_10), .out_9(out_3), .in_6(M1));
  Pull_Resistor pull_resistor_1 (.node(main_2_out_10));
  not not_1 (not_1_out, clock_2_out);
  S_R_Flip_Flop #(.trigger("high")) s_r_ff_1 (
    .S(main_2_out_10), .clk(1'b1), .R(START_out), .Q(koniec_gry));  // open: Qn, preset, reset, en
  \Sterowanie_dużo  \sterowanie_dużo_1  (
    .Wejscie_Klawiatury(keyboard_1_data), .Nr_Zaznaczonego_pola(\sterowanie_dużo_1_nr_zaznaczonego_pola ),
    .Enter(E1), .M(M1), .X(X1), .Y(Y1));
  RAM #(.addrWidth(4), .dataWidth(4), .bus("asynch")) ram_1 (
    .addr(Adres), .data(ram_1_data), .sel(1'b1), .ld(not_1_out));  // open: clr
  assign ram_1_data = clock_2_out ? out_2 : 4'bz;  // Controlled_Buffer controlled_buffer_1
  not not_2 (not_2_out, clock_2_out);
  assign controlled_buffer_2_out = not_2_out ? ram_1_data : 4'bz;  // Controlled_Buffer controlled_buffer_2
  Button START (.out(START_out));
  DotMatrix #(.inputtype("row"), .matrixcols(31), .matrixrows(31)) dotmatrix_1 (
    .row0(main_3_out_7), .row1(main_3_out_8), .row2(main_3_out_9), .row3(main_3_out_10),
    .row4(main_3_out_11), .row5(main_3_out_12), .row6(main_3_out_13), .row7(main_3_out_14),
    .row8(main_3_out_15), .row9(main_3_out_16), .row10(main_3_out_17), .row11(main_3_out_18),
    .row12(main_3_out_19), .row13(main_3_out_20), .row14(main_3_out_21), .row15(main_3_out_22),
    .row16(main_3_out_23), .row17(main_3_out_24), .row18(main_3_out_25), .row19(main_3_out_26),
    .row20(main_3_out_27), .row21(main_3_out_28), .row22(main_3_out_29), .row23(main_3_out_30),
    .row24(main_3_out_31), .row25(main_3_out_32), .row26(main_3_out_33), .row27(main_3_out_34),
    .row28(main_3_out_35), .row29(main_3_out_36), .row30(main_3_out_37));
  SAPER2_main main_3 (
    .x(X1), .Y(Y1), .WYJSCIE(controlled_buffer_2_out), .START(START_out),
    .PAMIEC(\sterowanie_dużo_1_nr_zaznaczonego_pola ), .ENTER(E1), .out_7(main_3_out_7),
    .out_8(main_3_out_8), .out_9(main_3_out_9), .out_10(main_3_out_10), .out_11(main_3_out_11),
    .out_12(main_3_out_12), .out_13(main_3_out_13), .out_14(main_3_out_14), .out_15(main_3_out_15),
    .out_16(main_3_out_16), .out_17(main_3_out_17), .out_18(main_3_out_18), .out_19(main_3_out_19),
    .out_20(main_3_out_20), .out_21(main_3_out_21), .out_22(main_3_out_22), .out_23(main_3_out_23),
    .out_24(main_3_out_24), .out_25(main_3_out_25), .out_26(main_3_out_26), .out_27(main_3_out_27),
    .out_28(main_3_out_28), .out_29(main_3_out_29), .out_30(main_3_out_30), .out_31(main_3_out_31),
    .out_32(main_3_out_32), .out_33(main_3_out_33), .out_34(main_3_out_34), .out_35(main_3_out_35),
    .out_36(main_3_out_36), .out_37(main_3_out_37));
endmodule
