// Logisim project porównywacz.circ as structural Verilog: 1 circuit, main circuit main
module main (
  input  [1:0] in_1,
  input  [5:0] in_2,
  input  in_3,
  input  [4:0] in_4,
  input  [4:0] in_5,
  input  in_6,
  input  in_7,
  output [3:0] out_8,
  output [5:0] out_9,
  output out_10
);

  wire and_3_out, and_4_out, clock_1_out, clock_2_out, clock_3_out, clock_4_out, clock_5_out, clock_6_out,
       clock_7_out, comparator_2_eq, comparator_3_eq, comparator_4_eq, comparator_5_eq, comparator_6_eq,
       comparator_7_eq, comparator_8_eq, comparator_9_eq, comparator_10_eq, controlled_buffer_1_out,
       controlled_buffer_2_out, not_1_out, not_2_out, not_3_out, not_4_out, not_5_out, or_2_out, RZE, S1, S4,
       s_r_ff_4_q, Z1, Z4, Z5;
  wire [1:0] and_2_out, counter_3_q, or_1_out;
  wire [1:1] K1;
  wire [3:0] adder_1_out, adder_2_out, adder_3_out, adder_4_out, adder_5_out, adder_6_out, adder_7_out,
       counter_4_q, counter_5_q, counter_6_q, counter_7_q, counter_8_q, counter_9_q, counter_10_q,
       counter_11_q;
  wire [5:0] controlled_buffer_3_out, D1, D2, D3, D4, D5, D6, D7, D8, ram_1_data;

  Clock clock_1 (.out(clock_1_out));
  Clock clock_2 (.out(clock_2_out));
  Clock clock_3 (.out(clock_3_out));
  Clock clock_4 (.out(clock_4_out));
  not not_1 (not_1_out, in_3);
  assign controlled_buffer_1_out = not_1_out ? clock_1_out : 1'bz;  // Controlled_Buffer controlled_buffer_1
  S_R_Flip_Flop s_r_ff_1 (.S(S1), .clk(clock_2_out), .R(in_3), .Q(K1[1]));  // open: Qn, preset, reset, en
  not not_2 (not_2_out, in_7);
  assign controlled_buffer_2_out = not_2_out ? clock_3_out : 1'bz;  // Controlled_Buffer controlled_buffer_2
  S_R_Flip_Flop s_r_ff_2 (.S(Z1), .clk(clock_4_out), .R(in_7), .Q(Z5));  // open: Qn, preset, reset, en
  Pull_Resistor pull_resistor_1 (.node(controlled_buffer_1_out));
  nand nand_1 (S4, controlled_buffer_1_out, ~K1[1]);  // NAND_Gate
  Pull_Resistor pull_resistor_2 (.node(controlled_buffer_2_out));
  and and_1 (Z4, controlled_buffer_2_out, ~Z5);  // AND_Gate
  Counter #(.width(4), .max('h8), .trigger("falling")) counter_1 (
    .load(1'b1), .carry(S1), .clk(S4));  // open: D, count, Q, clr
  Counter #(.width(4), .max('h4), .trigger("falling")) counter_2 (
    .load(1'b1), .carry(Z1), .clk(Z4));  // open: D, count, Q, clr
  assign and_2_out = in_1 & ~{2{K1[1]}};  // AND_Gate and_2, 2 bits wide
  assign or_1_out = and_2_out | counter_3_q;  // OR_Gate or_1, 2 bits wide
  and and_3 (and_3_out, ~K1[1], S4);  // AND_Gate
  Comparator #(.width(6)) comparator_1 (.a(out_9), .b(controlled_buffer_3_out), .eq(out_10));  // open: gt, lt
  Counter #(.width(2), .max('h2), .ongoal("continue"), .trigger("falling")) counter_3 (
    .Q(counter_3_q), .clk(Z4), .clr(Z5));  // open: load, D, count, carry
  Clock clock_5 (.out(clock_5_out));
  not not_3 (not_3_out, and_3_out);
  Uklad_zwracania_pozycji_sasiednich_bitow uklad_zwracania_pozycji_sasiednich_bitow_1 (
    .Input_Y(in_4), .Input_X(in_5), .LG(D1), .G(D2), .P(D4), .DP(D5), .D(D6), .LD(D7), .L(D8),
    .O_X(out_9[2:0]), .O_Y(out_9[5:3]), .PG(D3));
  RAM #(.addrWidth(2), .dataWidth(6), .bus("separate")) ram_1 (
    .addr(or_1_out), .din(in_2), .data(ram_1_data), .str(and_3_out), .sel(1'b1), .clk(clock_5_out), .clr(in_3));  // open: ld
  Clock clock_6 (.out(clock_6_out));
  assign controlled_buffer_3_out = RZE ? ram_1_data : 6'bz;  // Controlled_Buffer controlled_buffer_3
  S_R_Flip_Flop s_r_ff_3 (.S(in_7), .clk(clock_6_out), .R(Z1), .Q(RZE));  // open: Qn, preset, reset, en
  Counter #(.width(4), .max('hf), .trigger("falling")) counter_4 (
    .Q(counter_4_q), .clk(comparator_2_eq), .clr(in_7));  // open: load, D, count, carry
  Comparator #(.width(6)) comparator_2 (.a(D1), .b(controlled_buffer_3_out), .eq(comparator_2_eq));  // open: gt, lt
  Counter #(.width(4), .max('hf), .trigger("falling")) counter_5 (
    .Q(counter_5_q), .clk(comparator_3_eq), .clr(in_7));  // open: load, D, count, carry
  Comparator #(.width(6)) comparator_3 (.a(D2), .b(controlled_buffer_3_out), .eq(comparator_3_eq));  // open: gt, lt
  Counter #(.width(4), .max('hf), .trigger("falling")) counter_6 (
    .Q(counter_6_q), .clk(comparator_4_eq), .clr(in_7));  // open: load, D, count, carry
  Comparator #(.width(6)) comparator_4 (.a(D3), .b(controlled_buffer_3_out), .eq(comparator_4_eq));  // open: gt, lt
  Counter #(.width(4), .max('hf), .trigger("falling")) counter_7 (
    .Q(counter_7_q), .clk(comparator_5_eq), .clr(in_7));  // open: load, D, count, carry
  Comparator #(.width(6)) comparator_5 (.a(D4), .b(controlled_buffer_3_out), .eq(comparator_5_eq));  // open: gt, lt
  Counter #(.width(4), .max('hf), .trigger("falling")) counter_8 (
    .Q(counter_8_q), .clk(comparator_6_eq), .clr(in_7));  // open: load, D, count, carry
  Comparator #(.width(6)) comparator_6 (.a(D5), .b(controlled_buffer_3_out), .eq(comparator_6_eq));  // open: gt, lt
  Counter #(.width(4), .max('hf), .trigger("falling")) counter_9 (
    .Q(counter_9_q), .clk(comparator_7_eq), .clr(in_7));  // open: load, D, count, carry
  Comparator #(.width(6)) comparator_7 (.a(D6), .b(controlled_buffer_3_out), .eq(comparator_7_eq));  // open: gt, lt
  Counter #(.width(4), .max('hf), .trigger("falling")) counter_10 (
    .Q(counter_10_q), .clk(comparator_8_eq), .clr(in_7));  // open: load, D, count, carry
  Comparator #(.width(6)) comparator_8 (.a(D7), .b(controlled_buffer_3_out), .eq(comparator_8_eq));  // open: gt, lt
  Counter #(.width(4), .max('hf), .trigger("falling")) counter_11 (
    .Q(counter_11_q), .clk(comparator_9_eq), .clr(in_7));  // open: load, D, count, carry
  Comparator #(.width(6)) comparator_9 (.a(D8), .b(controlled_buffer_3_out), .eq(comparator_9_eq));  // open: gt, lt
  Adder #(.width(4)) adder_1 (.a(counter_4_q), .b(counter_5_q), .out(adder_1_out));  // open: cin, cout
  Adder #(.width(4)) adder_2 (.a(counter_6_q), .b(counter_7_q), .out(adder_2_out));  // open: cin, cout
  Adder #(.width(4)) adder_3 (.a(counter_8_q), .b(counter_9_q), .out(adder_3_out));  // open: cin, cout
  Adder #(.width(4)) adder_4 (.a(counter_10_q), .b(counter_11_q), .out(adder_4_out));  // open: cin, cout
  Adder #(.width(4)) adder_5 (.a(adder_1_out), .b(adder_2_out), .out(adder_5_out));  // open: cin, cout
  Adder #(.width(4)) adder_6 (.a(adder_3_out), .b(adder_4_out), .out(adder_6_out));  // open: cin, cout
  Adder #(.width(4)) adder_7 (.a(adder_5_out), .b(adder_6_out), .out(adder_7_out));  // open: cin, cout
  assign out_8 = not_4_out ? adder_7_out : 4'bz;  // Controlled_Buffer controlled_buffer_4
  not not_4 (not_4_out, s_r_ff_4_q);
  Comparator #(.width(4)) comparator_10 (.a(adder_7_out), .b(4'b0000), .eq(comparator_10_eq));  // open: gt, lt
  not not_5 (not_5_out, comparator_10_eq);
  or or_2 (or_2_out, not_5_out, in_6);
  and and_4 (and_4_out, in_7, comparator_10_eq);
  Clock clock_7 (.out(clock_7_out));
  assign out_8 = s_r_ff_4_q ? 4'b1001 : 4'bz;  // Controlled_Buffer controlled_buffer_5
  S_R_Flip_Flop s_r_ff_4 (
    .S(and_4_out), .clk(clock_7_out), .R(or_2_out), .Q(s_r_ff_4_q));  // open: Qn, preset, reset, en

  // Other names for the same wires on the sheet: K1[0] = K1[1]; S5 = K1[1]; S2 = in_3; Z2 = in_7
endmodule
