// Logisim project Saper.circ as structural Verilog: 1 circuit, main circuit main
module main (
);

  wire clock_1_out, clock_2_out, clock_3_out, Enter, Koniec, Loss, M, not_1_out, Reset, Win;
  wire [1:0] DISP, DISP2, main_4_zegar;
  wire [2:0] uklad_zmiany_sterowania_z_3bit_na_5bit_1_out_x__3bit,
       uklad_zmiany_sterowania_z_3bit_na_5bit_1_out_xy_3bit;
  wire [3:0] V;
  wire [4:0] main_2_out_5, main_2_out_6, main_2_out_7, main_2_out_8, main_2_out_9, main_2_out_10,
       main_2_out_11, main_2_out_12, main_2_out_13, main_2_out_14, main_2_out_15, main_2_out_16,
       main_2_out_17, main_2_out_18, main_2_out_19, main_2_out_20, main_2_out_21, main_2_out_22,
       main_2_out_23, main_2_out_24, main_2_out_25, main_2_out_26, main_2_out_27, main_2_out_28,
       main_2_out_29, main_2_out_30, main_2_out_31, main_2_out_32, main_2_out_33, main_2_out_34,
       main_2_out_35, wyswietlacz_czasu_1_o0, wyswietlacz_czasu_1_o1, wyswietlacz_czasu_1_o2,
       wyswietlacz_czasu_1_o3, wyswietlacz_czasu_1_o4, wyswietlacz_czasu_1_o5, wyswietlacz_czasu_1_o6,
       wyswietlacz_czasu_1_o7, wyswietlacz_czasu_1_o8, wyswietlacz_czasu_1_o9, wyswietlacz_czasu_1_o10,
       wyswietlacz_czasu_1_o11, wyswietlacz_czasu_1_o12, wyswietlacz_czasu_1_o13, wyswietlacz_czasu_1_o14,
       wyswietlacz_czasu_1_o15, wyswietlacz_czasu_1_o16, wyswietlacz_czasu_1_o17, wyswietlacz_czasu_1_o18,
       wyswietlacz_czasu_1_o19, wyswietlacz_czasu_1_o20, X5, Y5;
  wire [5:0] main_4_dane;
  wire [6:0] controlled_buffer_1_out, Klawiatura;
  wire [11:0] L;
  wire [24:0] S_25b;
  wire [30:0] main_1_out_8, main_1_out_9, main_1_out_10, main_1_out_11, main_1_out_12, main_1_out_13,
       main_1_out_14, main_1_out_15, main_1_out_16, main_1_out_17, main_1_out_18, main_1_out_19,
       main_1_out_20, main_1_out_21, main_1_out_22, main_1_out_23, main_1_out_24, main_1_out_25,
       main_1_out_26, main_1_out_27, main_1_out_28, main_1_out_29, main_1_out_30, main_1_out_31,
       main_1_out_32, main_1_out_33, main_1_out_34, main_1_out_35, main_1_out_36, main_1_out_37,
       main_1_out_38;

  Button button_1 (.out(DISP2[1]));
  Button button_2 (.out(Reset));
  SAPER2_main main_1 (
    .x(X5), .Y(Y5), .WYJSCIE(V), .START(DISP2[1]), .PAMIEC(S_25b), .ENTER(Enter), .lose(Loss),
    .out_8(main_1_out_8), .out_9(main_1_out_9), .out_10(main_1_out_10), .out_11(main_1_out_11),
    .out_12(main_1_out_12), .out_13(main_1_out_13), .out_14(main_1_out_14), .out_15(main_1_out_15),
    .out_16(main_1_out_16), .out_17(main_1_out_17), .out_18(main_1_out_18), .out_19(main_1_out_19),
    .out_20(main_1_out_20), .out_21(main_1_out_21), .out_22(main_1_out_22), .out_23(main_1_out_23),
    .out_24(main_1_out_24), .out_25(main_1_out_25), .out_26(main_1_out_26), .out_27(main_1_out_27),
    .out_28(main_1_out_28), .out_29(main_1_out_29), .out_30(main_1_out_30), .out_31(main_1_out_31),
    .out_32(main_1_out_32), .out_33(main_1_out_33), .out_34(main_1_out_34), .out_35(main_1_out_35),
    .out_36(main_1_out_36), .out_37(main_1_out_37), .out_38(main_1_out_38), .Win(Win));
  DotMatrix #(.inputtype("row"), .matrixcols(31), .matrixrows(31)) dotmatrix_1 (
    .row0(main_1_out_8), .row1(main_1_out_9), .row2(main_1_out_10), .row3(main_1_out_11),
    .row4(main_1_out_12), .row5(main_1_out_13), .row6(main_1_out_14), .row7(main_1_out_15),
    .row8(main_1_out_16), .row9(main_1_out_17), .row10(main_1_out_18), .row11(main_1_out_19),
    .row12(main_1_out_20), .row13(main_1_out_21), .row14(main_1_out_22), .row15(main_1_out_23),
    .row16(main_1_out_24), .row17(main_1_out_25), .row18(main_1_out_26), .row19(main_1_out_27),
    .row20(main_1_out_28), .row21(main_1_out_29), .row22(main_1_out_30), .row23(main_1_out_31),
    .row24(main_1_out_32), .row25(main_1_out_33), .row26(main_1_out_34), .row27(main_1_out_35),
    .row28(main_1_out_36), .row29(main_1_out_37), .row30(main_1_out_38));
  lose_main main_2 (
    .in_3(DISP2), .\L__połączyć_z_L_z_licznika_czasu_main (L), .out_5(main_2_out_5), .out_6(main_2_out_6),
    .out_7(main_2_out_7), .out_8(main_2_out_8), .out_9(main_2_out_9), .out_10(main_2_out_10),
    .out_11(main_2_out_11), .out_12(main_2_out_12), .out_13(main_2_out_13), .out_14(main_2_out_14),
    .out_15(main_2_out_15), .out_16(main_2_out_16), .out_17(main_2_out_17), .out_18(main_2_out_18),
    .out_19(main_2_out_19), .out_20(main_2_out_20), .out_21(main_2_out_21), .out_22(main_2_out_22),
    .out_23(main_2_out_23), .out_24(main_2_out_24), .out_25(main_2_out_25), .out_26(main_2_out_26),
    .out_27(main_2_out_27), .out_28(main_2_out_28), .out_29(main_2_out_29), .out_30(main_2_out_30),
    .out_31(main_2_out_31), .out_32(main_2_out_32), .out_33(main_2_out_33), .out_34(main_2_out_34),
    .out_35(main_2_out_35), .in_1(Loss), .Wl_WY(Win));
  DotMatrix #(.matrixcols(31), .matrixrows(5)) dotmatrix_2 (
    .col0(main_2_out_5), .col1(main_2_out_6), .col2(main_2_out_7), .col3(main_2_out_8), .col4(main_2_out_9),
    .col5(main_2_out_10), .col6(main_2_out_11), .col7(main_2_out_12), .col8(main_2_out_13),
    .col9(main_2_out_14), .col10(main_2_out_15), .col11(main_2_out_16), .col12(main_2_out_17),
    .col13(main_2_out_18), .col14(main_2_out_19), .col15(main_2_out_20), .col16(main_2_out_21),
    .col17(main_2_out_22), .col18(main_2_out_23), .col19(main_2_out_24), .col20(main_2_out_25),
    .col21(main_2_out_26), .col22(main_2_out_27), .col23(main_2_out_28), .col24(main_2_out_29),
    .col25(main_2_out_30), .col26(main_2_out_31), .col27(main_2_out_32), .col28(main_2_out_33),
    .col29(main_2_out_34), .col30(main_2_out_35));
  Keyboard keyboard_1 (.clk(clock_1_out), .data(Klawiatura));  // open: re, clr, avail
  Clock clock_1 (.out(clock_1_out));
  assign controlled_buffer_1_out = not_1_out ? Klawiatura : 7'bz;  // Controlled_Buffer controlled_buffer_1
  not not_1 (not_1_out, Koniec);
  Clock clock_2 (.out(clock_2_out));
  \Sterowanie_dużo  \sterowanie_dużo_1  (
    .Wejscie_Klawiatury(controlled_buffer_1_out), .Nr_Zaznaczonego_pola(S_25b), .Enter(Enter), .M(M), .X(X5),
    .Y(Y5));
  Pull_Resistor pull_resistor_1 (.node(DISP2[0]));
  assign DISP2[0] = Win ? clock_2_out : 1'bz;  // Controlled_Buffer controlled_buffer_2
  or or_1 (Koniec, Win, Loss);
  Clock #(.highDuration(32), .lowDuration(32)) clock_3 (.out(clock_3_out));
  DotMatrix #(.matrixcols(21), .matrixrows(5)) dotmatrix_3 (
    .col0(wyswietlacz_czasu_1_o20), .col1(wyswietlacz_czasu_1_o19), .col2(wyswietlacz_czasu_1_o18),
    .col3(wyswietlacz_czasu_1_o17), .col4(wyswietlacz_czasu_1_o16), .col5(wyswietlacz_czasu_1_o15),
    .col6(wyswietlacz_czasu_1_o14), .col7(wyswietlacz_czasu_1_o13), .col8(wyswietlacz_czasu_1_o12),
    .col9(wyswietlacz_czasu_1_o11), .col10(wyswietlacz_czasu_1_o10), .col11(wyswietlacz_czasu_1_o9),
    .col12(wyswietlacz_czasu_1_o8), .col13(wyswietlacz_czasu_1_o7), .col14(wyswietlacz_czasu_1_o6),
    .col15(wyswietlacz_czasu_1_o5), .col16(wyswietlacz_czasu_1_o4), .col17(wyswietlacz_czasu_1_o3),
    .col18(wyswietlacz_czasu_1_o2), .col19(wyswietlacz_czasu_1_o1), .col20(wyswietlacz_czasu_1_o0));
  wyswietlacz_czasu wyswietlacz_czasu_1 (
    .DISP_IN__1bit_reset_0bit_clk(DISP), .o0(wyswietlacz_czasu_1_o0), .o1(wyswietlacz_czasu_1_o1),
    .o2(wyswietlacz_czasu_1_o2), .o3(wyswietlacz_czasu_1_o3), .o4(wyswietlacz_czasu_1_o4),
    .o9(wyswietlacz_czasu_1_o9), .o8(wyswietlacz_czasu_1_o8), .o7(wyswietlacz_czasu_1_o7),
    .o6(wyswietlacz_czasu_1_o6), .o5(wyswietlacz_czasu_1_o5), .o15(wyswietlacz_czasu_1_o15),
    .o14(wyswietlacz_czasu_1_o14), .o13(wyswietlacz_czasu_1_o13), .o12(wyswietlacz_czasu_1_o12),
    .o11(wyswietlacz_czasu_1_o11), .o20(wyswietlacz_czasu_1_o20), .o19(wyswietlacz_czasu_1_o19),
    .o18(wyswietlacz_czasu_1_o18), .o17(wyswietlacz_czasu_1_o17), .o16(wyswietlacz_czasu_1_o16),
    .o10(wyswietlacz_czasu_1_o10));
  licznik_czasu_main main_3 (.Czas(L), .CLK(clock_3_out), .Stop(Koniec), .Start(DISP2[1]), .out_5(DISP));
  Maszyna_Los_XY22_main main_4 (.START(DISP2[1]), .DANE(main_4_dane), .ZEGAR(main_4_zegar));
  \porównywacz_main  main_5 (
    .in_1(main_4_zegar), .in_2(main_4_dane), .in_3(DISP2[1]), .in_6(Enter), .out_8(V),
    .Y(uklad_zmiany_sterowania_z_3bit_na_5bit_1_out_x__3bit),
    .X(uklad_zmiany_sterowania_z_3bit_na_5bit_1_out_xy_3bit), .out_9(Loss), .RESET(Reset));
  Uklad_zmiany_sterowania_z_3bit_na_5bit uklad_zmiany_sterowania_z_3bit_na_5bit_1 (
    .IN_X_5bit(X5), .IN_Y_5bit(Y5), .OUT_X__3bit(uklad_zmiany_sterowania_z_3bit_na_5bit_1_out_x__3bit),
    .OUT_XY_3bit(uklad_zmiany_sterowania_z_3bit_na_5bit_1_out_xy_3bit));

  // Other names for the same wires on the sheet: Start = DISP2[1]

  // Notes on the sheet:
  //   Aby rozpocząć rozgrywkę trzeba kliknąć start i poczekać z 5 sekundy aż bomby się ustawią
  //   Symulacja 128Hz
endmodule
